# Fritzing sketch SmartGardenUNO (saved by Fritzing 0.9.2b)
breadboards: 1

parts:
  Componente1 = Arduino Uno (Rev3)
  PART1 = SparkFun Soil Moisture Sensor [part_number=SEN-13322]
  U1 = ESP8266 WiFi Module [part_number=ESP8266]
  KY-1 = Keyes Relay [package=THT]
  M1 = DC Motor [part_number=RS-360SH]
  VCC1 = Battery
  R1 = Resistor [tolerance=±5% resistance=1 package=THT]
  R2 = Resistor [tolerance=±5% resistance=10 package=THT]
  R3 = Resistor [tolerance=±5% resistance=10 package=THT]

nets:
  N1: Componente1.A0, PART1.SIG
  N2: Componente1.D8, KY-1.signal
  N3: Componente1.D2, U1.TXD
  N4: Componente1.D3_PWM, R2.Pin_0
  VCC: Componente1.5V, PART1.VCC, U1.VCC, KY-1.power, R1.Pin_0, R3.Pin_1
  GND: Componente1.GND, PART1.GND, U1.GND, KY-1.ground
  N5: U1.RXD, R2.Pin_1, R3.Pin_0
  N6: U1.CH_PD, R1.Pin_1
  N7: KY-1.C, M1.pin_1
  N8: KY-1.NO, VCC1.+
  N9: M1.pin_2, VCC1.-

custom parts:
  SparkFun Soil Moisture Sensor: The SparkFun Soil Moisture Sensor is a simple breakout for measuring the moisture in soil and similar materials.
  ESP8266 WiFi Module: Generic WiFi Module based on the ESP8266 with onboard PCB antenna and UART communications
  Keyes Relay: The Keyes 5V relay module is suitable for SCM development, home appliance control. It uses a 5V~12V TIL control signal which can control DC / AC signal.
